# Fritzing sketch ledmatrix (saved by Fritzing 0.9.0b)
circuit board: 8.46667cm x 5.64444cm
breadboards: 1

parts:
  R1 = Resistor [tolerance=±5% resistance=220 package=THT]
  LED1 = LED - 5mm [color="Red (633nm)" package="5 mm [THT]"]
  V1 = DC Power [voltage=5]  # not connected
  U1 = atmega328 [package=dip]
  S3 = Pushbutton [package="[SMD]"]
  R2 = Resistor [tolerance=±5% resistance=10k package=THT]
  C1 = Electrolytic Capacitor [capacitance=10µF package="100 mil [THT, electrolytic]"]
  XTAL1 = Crystal [frequency="16 Mhz" package=THT]
  LED2 = LED - 5mm [color="Yellow (595nm)" package="5 mm [THT]"]
  C2 = Ceramic Capacitor [capacitance="100 nF" package="1206 [SMD, multilayer]"]
  C3 = Ceramic Capacitor [capacitance="100 nF" package="1206 [SMD, multilayer]"]
  R3 = Resistor [tolerance=±5% resistance=220 package=THT]
  U2 = 74HC595 [package="DIP16 [THT]"]  # not connected
  U3 = 74HC595 [package="DIP16 [THT]"]  # not connected
  R4 = Resistor [tolerance=±5% resistance=250 package=THT]  # not connected
  R5 = Resistor [tolerance=±5% resistance=250 package=THT]  # not connected
  R6 = Resistor [tolerance=±5% resistance=250 package=THT]  # not connected
  R7 = Resistor [tolerance=±5% resistance=250 package=THT]  # not connected
  R8 = Resistor [tolerance=±5% resistance=250 package=THT]  # not connected
  R9 = Resistor [tolerance=±5% resistance=250 package=THT]  # not connected
  R10 = Resistor [tolerance=±5% resistance=250 package=THT]  # not connected
  R11 = Resistor [tolerance=±5% resistance=250 package=THT]  # not connected
  U4 = mystery part, 24 pins [chip_label=?]

nets (from the breadboard view):
  N1: R1.Pin_0, LED1.anode
  N2: R1.Pin_1, U1.VCC, U1.AVCC, S3.Pin_3, S3.Pin_4, R2.Pin_1, C1.+
  N3: LED1.cathode, U1.GND, C1.-, LED2.cathode, C2.1, C3.0
  N4: U1.RESET, S3.Pin_1, S3.Pin_2, R2.Pin_0
  N5: U1.XLAT1, XTAL1.pin_0, C3.1
  N6: U1.XLAT2, XTAL1.pin_1, C2.0
  N7: U1.D13, R3.Pin_1
  N8: LED2.anode, R3.Pin_0
  N9: U4.pin1, U4.pin24
  N10: U4.pin2, U4.pin23
  N11: U4.pin3, U4.pin22
  N12: U4.pin4, U4.pin21
  N13: U4.pin5, U4.pin20
  N14: U4.pin6, U4.pin19
  N15: U4.pin7, U4.pin18
  N16: U4.pin8, U4.pin17
  N17: U4.pin9, U4.pin16
  N18: U4.pin10, U4.pin15
  N19: U4.pin11, U4.pin14
  N20: U4.pin12, U4.pin13
